# Fritzing sketch Projet-IoT (saved by Fritzing 0.9.4)
circuit board: 8.46667cm x 5.64444cm
breadboards: 1

parts:
  U1 = ESP8266 WiFi Module [part_number=ESP8266]
  R1 = PHOTOCELL [package=photocell-kit]
  R2 = Resistor [tolerance=±5% resistance=220 package="1206 [SMD]"]
  RHT1 = Humidity and Temperature Sensor RHT03
  R3 = Resistor [tolerance=±5% resistance=220 package="1206 [SMD]"]

nets:
  N1: U1.D0, RHT1.Data-signal, R3.Pin_0
  N2: U1.IO15, R1.P$1, R2.Pin_1
  N3: U1.GND, R2.Pin_0, RHT1.GND_2
  3.3V: U1.3.3V, R1.P$2, RHT1.Vcc, R3.Pin_1
